# Fritzing sketch analog-diy (saved by Fritzing 0.9.3b)
circuit board: 4.5cm x 3cm
breadboards: 1

parts:
  841 = SOIC-14 [chip_label=SOIC-14 package=SO]
  XBee = XBee
  R1 = Resistor [tolerance=±5% resistance=5k package=THT]
  C1 = Tantalum Capacitor [capacitance=1μF package="100 mil [THT, tantalum]"]
  Joystick = female pin header, 5 pins [form="♀ (female)"]
  GND_VCC = female pin header, 7 pins [form="♀ (female)"]

nets:
  N1: 841.1, 841.13, XBee.VCC, XBee.pin14, R1.Pin_1, C1.+, Joystick.pin2, GND_VCC.pin2
  N2: 841.4, R1.Pin_0, GND_VCC.pin3
  N3: 841.5, Joystick.pin3
  N4: 841.7, Joystick.pin4, GND_VCC.pin4
  N5: 841.8, XBee.pin19, GND_VCC.pin6
  N6: 841.9, XBee.pin18, GND_VCC.pin7
  N7: 841.10, XBee.pin17
  N8: 841.11, XBee.pin11
  N9: 841.12, GND_VCC.pin5
  N10: 841.14, XBee.GND, C1.-, Joystick.pin1, GND_VCC.pin1
  N11: XBee.pin15, Joystick.pin5

notes:
  tjlepp@gmail.com

custom parts:
  XBee: XBee embedded RF module.
