# Fritzing sketch sender (saved by Fritzing 0.9.3b)
circuit board: 5.2cm x 4.5cm
breadboards: 1

parts:
  XBee = XBEE-1 [package=xbee-silk]
  GND_VCC = female pin header, 2 pins [form="♀ (female)"]
  3_3V = Voltage Regulator - 3.3V [package="TO220 [THT]"]
  Joystick = DB9 Connector [package=db9]
  C1 = Tantalum Capacitor [capacitance=1μF package="100 mil [THT, tantalum]"]
  C2 = Tantalum Capacitor [capacitance=1μF package="100 mil [THT, tantalum]"]
  C3 = Tantalum Capacitor [capacitance=1μF package="100 mil [THT, tantalum]"]
  5V = Voltage Regulator - 5V [package="DPak [SMD]"]
  BOB-12009 = IC, DIP package, 12 pins [chip_label=IC]
  BOB-12009_2 = IC, DIP package, 12 pins [chip_label=IC]

nets:
  N1: XBee.VDD, XBee.RES, 3_3V.output_voltage, C3.+, BOB-12009.pin3, BOB-12009_2.pin3
  GND: XBee.GND, GND_VCC.pin1, 3_3V.GND, Joystick.8, C1.-, C2.-, C3.-, 5V.GND, BOB-12009.pin4, BOB-12009.pin9, BOB-12009_2.pin4, BOB-12009_2.pin9
  N2: XBee.DIO4, BOB-12009_2.pin2
  N3: XBee.DIO5, BOB-12009_2.pin5
  N4: XBee.DIO3, BOB-12009_2.pin1
  N5: XBee.DIO2, BOB-12009.pin6
  N6: XBee.DIO1, BOB-12009.pin5
  N7: XBee.DIO0, BOB-12009.pin2
  N8: GND_VCC.pin2, C1.+, 5V.input_voltage
  N9: 3_3V.input_voltage, Joystick.7, C2.+, 5V.output_voltage, BOB-12009.pin10, BOB-12009_2.pin10
  N10: Joystick.1, BOB-12009_2.pin11
  N11: Joystick.2, BOB-12009_2.pin12
  N12: Joystick.3, BOB-12009.pin7
  N13: Joystick.4, BOB-12009.pin8
  N14: Joystick.6, BOB-12009_2.pin8
  N15: Joystick.9, BOB-12009.pin11

notes:
  tjlepp 2017
  tjlepp@gmail.com
